// Logisim project cpu.circ as structural Verilog
module ALU (
  input  [3:0] A,
  input  [3:0] B,
  input  [3:0] OPcode,
  output [3:0] Y,
  output O,
  output Cout,
  output Z,
  output N
);

  wire [3:0] four_bit_full_adder_1_sum, logic_unit_1_y;

  four_bit_full_adder four_bit_full_adder_1 (
    .A(A), .Cin(OPcode[0]), .B(B), .Sum(four_bit_full_adder_1_sum), .O(O), .Cout(Cout));
  logic_unit logic_unit_1 (.a(A), .b(B), .f(OPcode[2:1]), .y(logic_unit_1_y));
  Multiplexer #(.width(4)) multiplexer_1 (
    .in0(four_bit_full_adder_1_sum), .in1(logic_unit_1_y), .out({N, Y[2:0]}), .sel(OPcode[3]));
  nor nor_1 (Z, Y[0], Y[1], Y[2], N);

  assign Y[3] = N;
endmodule

module four_bit_full_adder (
  input  [3:0] A,
  input  Cin,
  input  [3:0] B,
  output [3:0] Sum,
  output O,
  output Cout
);

  wire adder_1_cout, adder_2_cout, adder_3_cout, xor_1_out, xor_2_out, xor_3_out, xor_4_out;

  xor xor_1 (xor_1_out, B[0], Cin);
  xor xor_2 (xor_2_out, B[1], Cin);
  xor xor_3 (xor_3_out, B[2], Cin);
  xor xor_4 (xor_4_out, B[3], Cin);
  Adder #(.width(1)) adder_1 (.a(A[0]), .b(xor_1_out), .out(Sum[0]), .cin(Cin), .cout(adder_1_cout));
  Adder #(.width(1)) adder_2 (.a(A[1]), .b(xor_2_out), .out(Sum[1]), .cin(adder_1_cout), .cout(adder_2_cout));
  Adder #(.width(1)) adder_3 (.a(A[2]), .b(xor_3_out), .out(Sum[2]), .cin(adder_2_cout), .cout(adder_3_cout));
  Adder #(.width(1)) adder_4 (.a(A[3]), .b(xor_4_out), .out(Sum[3]), .cin(adder_3_cout), .cout(Cout));
  xor xor_5 (O, adder_3_cout, Cout);
endmodule

module logic_unit (
  input  [3:0] a,
  input  [3:0] b,
  input  [1:0] f,
  output [3:0] y
);

  wire [3:0] and_1_out, or_1_out, xor_1_out;

  assign and_1_out = a & b;  // AND_Gate and_1, 4 bits wide
  assign or_1_out = a | b;  // OR_Gate or_1, 4 bits wide
  assign xor_1_out = a ^ b;  // XOR_Gate xor_1, 4 bits wide
  Multiplexer #(.select(2), .width(4)) multiplexer_1 (
    .in0(and_1_out), .in1(or_1_out), .in2(xor_1_out), .in3(b), .out(y), .sel(f));
endmodule

// R3
module register_file (
  input  Clk,
  input  [3:0] In_Vale,
  input  Write,
  input  [2:0] Ra,
  input  [2:0] Rd,
  input  [2:0] Rb,
  input  Clear,
  output [3:0] OUT_A,
  output [3:0] OUT_B
);

  wire demultiplexer_1_out0, demultiplexer_1_out1, demultiplexer_1_out2, demultiplexer_1_out3,
       demultiplexer_1_out4, demultiplexer_1_out5, demultiplexer_1_out6, demultiplexer_1_out7;
  wire [3:0] R0_q, R1_q, R2_q, R3_q, R4_q, R5_q, R6_q, R7_q;

  Demultiplexer #(.select(3)) demultiplexer_1 (
    .out0(demultiplexer_1_out0), .out1(demultiplexer_1_out1), .out2(demultiplexer_1_out2),
    .out3(demultiplexer_1_out3), .out4(demultiplexer_1_out4), .out5(demultiplexer_1_out5),
    .out6(demultiplexer_1_out6), .out7(demultiplexer_1_out7), .in(Write), .sel(Rd));
  Register #(.width(4)) R0 (.D(In_Vale), .en(demultiplexer_1_out0), .clk(Clk), .Q(R0_q), .clr(Clear));
  Register #(.width(4)) R1 (.D(In_Vale), .en(demultiplexer_1_out1), .clk(Clk), .Q(R1_q), .clr(Clear));
  Register #(.width(4)) R2 (.D(In_Vale), .en(demultiplexer_1_out2), .clk(Clk), .Q(R2_q), .clr(Clear));
  Register #(.width(4)) R3 (.D(In_Vale), .en(demultiplexer_1_out3), .clk(Clk), .Q(R3_q), .clr(Clear));
  Register #(.width(4)) R4 (.D(In_Vale), .en(demultiplexer_1_out4), .clk(Clk), .Q(R4_q), .clr(Clear));
  Register #(.width(4)) R5 (.D(In_Vale), .en(demultiplexer_1_out5), .clk(Clk), .Q(R5_q), .clr(Clear));
  Register #(.width(4)) R6 (.D(In_Vale), .en(demultiplexer_1_out6), .clk(Clk), .Q(R6_q), .clr(Clear));
  Register #(.width(4)) R7 (.D(In_Vale), .en(demultiplexer_1_out7), .clk(Clk), .Q(R7_q), .clr(Clear));
  Multiplexer #(.select(3), .width(4)) multiplexer_1 (
    .in0(R0_q), .in1(R1_q), .in2(R2_q), .in3(R3_q), .in4(R4_q), .in5(R5_q), .in6(R6_q), .in7(R7_q),
    .out(OUT_A), .sel(Ra));
  Multiplexer #(.select(3), .width(4)) multiplexer_2 (
    .in0(R0_q), .in1(R1_q), .in2(R2_q), .in3(R3_q), .in4(R4_q), .in5(R5_q), .in6(R6_q), .in7(R7_q),
    .out(OUT_B), .sel(Rb));
endmodule

module CPU (
  output out_1,
  output out_2,
  output out_3,
  output out_4,
  output [3:0] out_5
);

  wire Clear, Clk, controlled_buffer_8_out, Data, Load, MoveImm, not_1_out, or_1_out, Store;
  wire [2:0] controlled_buffer_2_out, controlled_buffer_7_out, Rd;
  wire [3:0] alu_1_y, controlled_buffer_1_out, controlled_buffer_5_out, ram_1_dout, register_file_1_out_a,
       register_file_1_out_b;
  wire [5:0] Addr;
  wire [7:0] counter_1_q;
  wire [15:0] rom_1_data;
  wire [15:13] register_1_q;

  RAM #(.addrWidth(10), .dataWidth(4), .enables("line")) ram_1 (
    .addr({out_5, Addr}), .we(Store), .clk(Clk), .din(controlled_buffer_5_out), .dout(ram_1_dout));
  assign controlled_buffer_1_out = Load ? ram_1_dout : 4'bz;  // Controlled_Buffer controlled_buffer_1
  assign controlled_buffer_2_out = not_1_out ? Addr[2:0] : 3'bz;  // Controlled_Buffer controlled_buffer_2
  not not_1 (not_1_out, Store);
  assign controlled_buffer_2_out = Store ? Rd : 3'bz;  // Controlled_Buffer controlled_buffer_3
  assign controlled_buffer_1_out = MoveImm ? Addr[3:0] : 4'bz;  // Controlled_Buffer controlled_buffer_4
  assign controlled_buffer_5_out = Store ? register_file_1_out_b : 4'bz;  // Controlled_Buffer controlled_buffer_5
  Counter counter_1 (.clr(1'b0), .load(1'b0), .up(1'b1), .count(1'b1), .clk(Clk), .Q(counter_1_q));  // open: D, carry
  or or_1 (or_1_out, Data, Load, MoveImm);
  assign controlled_buffer_1_out = Data ? alu_1_y : 4'bz;  // Controlled_Buffer controlled_buffer_6
  assign controlled_buffer_7_out = or_1_out ? Rd : 3'bz;  // Controlled_Buffer controlled_buffer_7
  assign controlled_buffer_8_out = Clear ? 1'b1 : 1'bz;  // Controlled_Buffer controlled_buffer_8
  ROM #(.dataWidth(16)) rom_1 (.addr(counter_1_q), .data(rom_1_data));
  register_file register_file_1 (
    .Clk(Clk), .In_Vale(controlled_buffer_1_out), .Write(or_1_out), .Ra(Addr[5:3]),
    .Rd(controlled_buffer_7_out), .Rb(controlled_buffer_2_out), .Clear(controlled_buffer_8_out),
    .OUT_A(register_file_1_out_a), .OUT_B(register_file_1_out_b));
  Register #(.width(16)) register_1 (
    .D(rom_1_data), .en(1'b1), .clk(Clk), .Q({register_1_q, out_5, Addr, Rd}));  // open: clr
  Clock clock_1 (.out(Clk));
  ALU alu_1 (
    .A(register_file_1_out_a), .B(register_file_1_out_b), .OPcode(out_5), .Y(alu_1_y), .O(out_1),
    .Cout(out_2), .Z(out_3), .N(out_4));
  and and_1 (Data, register_1_q[13], ~register_1_q[14], ~register_1_q[15]);  // AND_Gate
  and and_2 (MoveImm, register_1_q[13], register_1_q[14], ~register_1_q[15]);  // AND_Gate
  and and_3 (Clear, register_1_q[13], register_1_q[14], register_1_q[15]);
  and and_4 (Load, ~register_1_q[13], ~register_1_q[14], register_1_q[15]);  // AND_Gate
  and and_5 (Store, register_1_q[13], ~register_1_q[14], register_1_q[15]);  // AND_Gate
  Hex_Digit_Display hex_digit_display_1 (.value(alu_1_y));  // open: dp

  // Other names for the same wires on the sheet: Rb[2:0] = Addr[2:0]; Value[3:0] = Addr[3:0]; Ra[2:0] = Addr[5:3];
  //   Addr[9:6] = out_5; OPcode[3:0] = out_5

  // Notes on the sheet:
  //   contents of rom_1 (hex, n*v repeats v):
  //   6019 6022 2054 60e3 311e 6016 2337 a03f
  //   MOVE
  //   ADD
  //   SUB
  //   OR
  //   AND
  //   XOR
  //   INSTRUCTION 
  //   MOVE #3 R1
  //   MOVE #4 R2
  //   ADD R1 R2 R4
  //   MOVE #12 R3
  //   AND R4 R3 R5
  //   MOVE #2 R6
  //   SUB R4 R6 R7
  //   Instructions Implemented
  //   BINARY FORMAT 
  //   0110000000011001
  //   0110000000100010
  //   0010000001010100
  //   0110000011100011
  //   0011000100011110
  //   0110000000010110
  //   0010001100110111
  //   HEXADECIMAL FORMAT
  //   6019H
  //   6022H
  //   2054H
  //   60E3H
  //   311E
  //   6016H
  //   2337H
endmodule
